// Digital circuit CPU.dig as structural Verilog
module CPU (
  input  clk
);

  wire A_LD_CDATA, A_OUT_CDATA, and_1_out, and_2_out, and_3_out, CDATA_TO_CADDRH, CDATA_TO_CADDRL,
       IR_LD_XDATA, MAR_LD_CADDR, MBR_LD_CDATA, MBR_LD_XDATA, MBR_OUT_CDATA, MBR_OUT_XDATA, MEM_LD_XDATA,
       MEM_OUT_XDATA, not_1_out, or_1_out, PC_INC, PC_OUT_CADDR, STASH_LD_CDATA, STASH_OUT_CDATA;
  wire [7:0] A, driver_5_out, IR, MBR, ROM_d;
  wire [15:0] add_1_s, driver_1_out, MAR, PC;

  Seven_Seg_Hex seven_seg_hex_1 (.d(MAR[11:8]), .dp(1'b0));
  Seven_Seg_Hex seven_seg_hex_2 (.d(MAR[15:12]), .dp(1'b0));
  Register #(.Bits(16)) u_PC (.D(add_1_s), .C(clk), .en(PC_INC), .Q(PC));
  Seven_Seg_Hex seven_seg_hex_3 (.d(MAR[3:0]), .dp(1'b0));
  Seven_Seg_Hex seven_seg_hex_4 (.d(MAR[7:4]), .dp(1'b0));
  assign driver_1_out = PC_OUT_CADDR ? PC : 16'bz;  // Driver driver_1
  Seven_Seg_Hex seven_seg_hex_5 (.d(MBR[3:0]), .dp(1'b0));
  Seven_Seg_Hex seven_seg_hex_6 (.d(MBR[7:4]), .dp(1'b0));
  Add #(.Bits(16)) add_1 (.a(PC), .b(16'h1), .c_i(1'b0), .s(add_1_s));  // open: c_o
  Seven_Seg_Hex seven_seg_hex_7 (.d(PC[15:12]), .dp(1'b0));
  Register #(.Bits(16)) u_MAR (.D(driver_1_out), .C(clk), .en(MAR_LD_CADDR), .Q(MAR));
  Seven_Seg_Hex seven_seg_hex_8 (.d(PC[7:4]), .dp(1'b0));
  Seven_Seg_Hex seven_seg_hex_9 (.d(PC[11:8]), .dp(1'b0));
  Seven_Seg_Hex seven_seg_hex_10 (.d(IR[7:4]), .dp(1'b0));
  Seven_Seg_Hex seven_seg_hex_11 (.d(PC[3:0]), .dp(1'b0));
  Seven_Seg_Hex seven_seg_hex_12 (.d(IR[3:0]), .dp(1'b0));
  and and_1 (and_1_out, MAR[15], MEM_OUT_XDATA);
  Seven_Seg_Hex seven_seg_hex_13 (.d(A[3:0]), .dp(1'b0));
  Seven_Seg_Hex seven_seg_hex_14 (.d(A[7:4]), .dp(1'b0));
  assign driver_1_out[15:8] = CDATA_TO_CADDRH ? driver_5_out : 8'bz;  // Driver driver_2
  assign driver_1_out[7:0] = CDATA_TO_CADDRL ? driver_5_out : 8'bz;  // Driver driver_3
  ROM #(.AddrBits(14), .Bits(8)) ROM (.A(MAR[13:0]), .sel(and_1_out), .D(ROM_d));
  or or_1 (or_1_out, MEM_LD_XDATA, MEM_OUT_XDATA);
  not not_1 (not_1_out, MAR[15]);
  Register #(.Bits(8)) u_MBR (.D(ROM_d), .C(clk), .en(MBR_LD_XDATA), .Q(MBR));
  and and_2 (and_2_out, or_1_out, not_1_out);
  and and_3 (and_3_out, MEM_LD_XDATA, clk);
  assign ROM_d = MBR_OUT_XDATA ? MBR : 8'bz;  // Driver driver_4
  assign driver_5_out = MBR_OUT_CDATA ? MBR : 8'bz;  // Driver driver_5
  // Control_Unit control_unit_1: pin names not known; wires that end beside it: 1'b0, 1'b0, 1'b0, 1'b0, IR, clk, PC_OUT_CADDR, MAR_LD_CADDR, IR_LD_XDATA, PC_INC, MBR_LD_XDATA, MBR_OUT_CDATA, A_LD_CDATA, MEM_OUT_XDATA, MEM_LD_XDATA, MBR_OUT_XDATA, MBR_LD_CDATA, A_OUT_CDATA
  RAMSinglePortSel #(.AddrBits(14), .isProgramMemory("true"), .Bits(8)) RAM (
    .A(MAR[13:0]), .CS(and_2_out), .WE(and_3_out), .OE(MEM_OUT_XDATA), .D(ROM_d));
  Register #(.Bits(8)) u_IR (.D(ROM_d), .C(clk), .en(IR_LD_XDATA), .Q(IR));
  Register #(.Bits(8)) u_A (.D(driver_5_out), .C(clk), .en(A_LD_CDATA), .Q(A));
  assign driver_5_out = A_OUT_CDATA ? A : 8'bz;  // Driver driver_6
  Register #(.Bits(8)) STASH (.D(driver_5_out), .C(clk), .en(STASH_LD_CDATA), .Q(A));
  assign driver_5_out = STASH_OUT_CDATA ? A : 8'bz;  // Driver driver_7

  // Other names for the same wires on the sheet: P0_Clock = clk

  // Notes on the sheet:
  //   CADDRl Bus
  //   MAR
  //   XADDR
  //   MBR
  //   High bit 
  //     set => ROM
  //     unset => RAM
  //   CADDRh Bus
  //   PC
  //   IR
  //   A
  //   contents of ROM (hex, n*v repeats v):
  //   a9,42
  //   PROBLEM - NEED LATCH HALF OF MBR AT A TIME - SOLN SPLIT MBR
  //   XDATA Bus
  //   CDATA Bus
endmodule
